# Fritzing sketch lcdgps (saved by Fritzing 0.9.10b)
stripboards: 1

parts:
  Mod1 = Raspberry Pi 4B
  Part1 = Adafruit PiRTC PCF8523 [part_number="Adafruit #3386"]
  Part2 = Standard LCD 16x2 white on blue [part_number=181]
  ENCODER1 = Rotary Encoder with Knob
  proto1 = Adafruit_PermaProto_1_4_Board
  POT1 = Breadboard Trimpot  # not connected
  S2 = Round Pushbutton
  LED2 = smd LED [color="Green (570nm)" package="1206 [SMD]"]
  LED3 = smd LED [color="Red (660nm)" package="1206 [SMD]"]
  LED1 = smd LED [color="Blue (470nm)" package="1206 [SMD]"]
  R1 = Resistor [tolerance=±5% power=0.25 resistance=220 package=THT]
  R2 = Resistor [tolerance=±5% power=0.25 resistance=220 package=THT]
  R3 = Resistor [tolerance=±5% power=0.25 resistance=220 package=THT]

nets:
  3V3: Mod1.3V3, Part1.3.3V
  5V: Mod1.5V, Part2.VDD, Part2.LED+, proto1.connectorB5, proto1.connectorE5, proto1.connectorY1, proto1.connectorY2, proto1.connectorY3, proto1.connectorY4, proto1.connectorY5, proto1.connectorY6, proto1.connectorY7, proto1.connectorY8, proto1.connectorY9, proto1.connectorY10, proto1.connectorY11, proto1.connectorY12, proto1.connectorY13, proto1.connectorY14, proto1.connectorY15
  N1: Mod1.GPIO2, Part1.SDA
  N2: Mod1.GPIO3, Part1.SCL
  GND: Mod1.GND, Part1.GND, Part2.VSS, Part2.R/W, Part2.LED-, ENCODER1.no_name_yet#2, ENCODER1.no_name_yet#4, proto1.connectorB3, proto1.connectorE3, proto1.connectorZ1, proto1.connectorZ2, proto1.connectorZ3, proto1.connectorZ4, proto1.connectorZ5, proto1.connectorZ6, proto1.connectorZ7, proto1.connectorZ8, proto1.connectorZ9, proto1.connectorZ10, proto1.connectorZ11, proto1.connectorZ12, proto1.connectorZ13, proto1.connectorZ14, proto1.connectorZ15, S2.leg0, R1.Pin_0, R2.Pin_0, R3.Pin_0
  N3: Mod1.GPIO17, Part2.E
  N4: Mod1.GPIO18, Part2.DB7
  N5: Mod1.GPIO22, Part2.RS
  N6: Mod1.GPIO23, Part2.DB6
  N7: Mod1.GPIO24, Part2.DB5
  N8: Mod1.GPIO25, Part2.DB4
  N9: Mod1.GPIO5, LED1.cathode
  N10: Mod1.GPIO6, LED2.cathode
  N11: Mod1.GPIO13, LED3.cathode
  N12: Mod1.GPIO19, S2.leg1
  N13: Mod1.GPIO16, ENCODER1.no_name_yet#5
  N14: Mod1.GPIO20, ENCODER1.no_name_yet#1
  N15: Mod1.GPIO21, ENCODER1.no_name_yet#3
  N16: Part2.V0, proto1.connectorB4, proto1.connectorE4
  N17: LED2.anode, R2.Pin_1
  N18: LED3.anode, R3.Pin_1
  N19: LED1.anode, R1.Pin_1

custom parts:
  Adafruit PiRTC PCF8523: This is a great battery-backed real time clock (RTC) that allows your Raspberry Pi project to keep track of time if the power is lost. Perfect for data-logging, clock-building, time-stamping, timers and alarms, etc. Equipped with PCF8523 RTC, it works great with the Raspberry Pi and has native kernel support. Works perfectly with any Raspberry Pi (or similar single board linux computer)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
  Standard LCD 16x2 white on blue: Standard HD44780 LCDs are useful for creating standalone projects. * 16 characters wide, 2 rows * White text on blue background * Connection port is 0.1" pitch, single row for easy breadboarding and wiring
  Rotary Encoder with Knob: Rotary Encoder with 1/4" Shaft and Knob
